# Fritzing sketch propellerhead (saved by Fritzing 0.9.2b)
circuit board: 9.87778cm x 6.71689cm
perfboards: 1

parts:
  MCP2025 = IC, DIP package, 8 pins [chip_label=2025]
  J1 = male pin header, 6 pins [form="♂ (male)"]
  Part2 = Gikfun Pro Mini
  Part3 = BC127 Breakout Board
  J2 = male pin header, 2 pins [form="♂ (male)"]

nets:
  N1: MCP2025.pin1, J1.pin1
  N2: MCP2025.pin3, J1.pin2
  N3: MCP2025.pin4, J1.pin3
  N4: MCP2025.pin5, Part2.D1/RX
  N5: MCP2025.pin6, Part2.D0/TX
  N6: MCP2025.pin8, Part2.VCC, Part3.V_BAT
  N7: J1.pin4, Part3.SP_RP
  N8: J1.pin5, Part3.SP_LP
  N9: J1.pin6, Part3.SP_LN
  GND: Part2.GND, Part3.GND
  N10: Part2.D11_PWM/MOSI, Part3.TX
  N11: Part2.D10_PWM/SS, Part3.RX
  N12: Part2.D6_PWM, J2.pin1
  N13: Part2.D5_PWM, J2.pin2

custom parts:
  Gikfun Pro Mini: It's blue! It's thin! It's the Arduino Pro Mini! SparkFun's minimal design approach to Arduino. This is a 5V Arduino running the 16MHz bootloader. Arduino Pro Mini does not come with connectors populated so that you can solder in any connector or wire with any orientation you need. We recommend first time Arduino users start with the Uno R3. It's a great board that will get you up and running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
